// Logisim project DZ.circ as structural Verilog
module \СКНФ  (
);

  wire _1_out, _2_out, _3_out, _4_out, _5_out, _6_out, _7_out, _8_out, and_1_out, and_2_out, and_3_out,
       and_4_out, and_5_out, and_6_out, and_7_out, not_1_out, not_2_out, not_3_out, not_4_out, or_1_out,
       or_2_out, or_3_out, or_4_out, or_5_out, or_6_out, or_7_out, x0_out, x1_out, x2_out, x3_out;

  Clock #(.highDuration(8), .lowDuration(8)) x3 (.out(x3_out));
  Clock #(.highDuration(4), .lowDuration(4)) x2 (.out(x2_out));
  Clock #(.highDuration(2), .lowDuration(2)) x1 (.out(x1_out));
  Clock x0 (.out(x0_out));
  not not_1 (not_1_out, x3_out);
  not not_2 (not_2_out, x2_out);
  not not_3 (not_3_out, x1_out);
  not not_4 (not_4_out, x0_out);
  or or_1 (or_1_out, not_1_out, not_2_out);
  or or_2 (or_2_out, not_2_out, x3_out);
  or or_3 (or_3_out, x3_out, x2_out);
  or or_4 (or_4_out, not_1_out, x2_out);
  or or_5 (or_5_out, not_3_out, x0_out);
  or or_6 (or_6_out, not_3_out, not_4_out);
  or or_7 (or_7_out, x1_out, not_4_out);
  or _7 (_7_out, or_1_out, or_5_out);
  or _3 (_3_out, or_2_out, or_7_out);
  or _1 (_1_out, or_3_out, or_5_out);
  or _2 (_2_out, or_3_out, or_6_out);
  or _4 (_4_out, or_2_out, or_5_out);
  or _5 (_5_out, or_5_out, or_4_out);
  or _6 (_6_out, or_4_out, or_6_out);
  or _8 (_8_out, or_1_out, or_6_out);
  and and_1 (and_1_out, _7_out, _3_out);
  and and_2 (and_2_out, _1_out, _2_out);
  and and_3 (and_3_out, _4_out, _5_out);
  and and_4 (and_4_out, _6_out, _8_out);
  and and_5 (and_5_out, and_1_out, and_2_out);
  and and_6 (and_6_out, and_3_out, and_4_out);
  LED led_1 (.in(and_7_out));
  and and_7 (and_7_out, and_5_out, and_6_out);
endmodule

module \МДНФ  (
);

  wire and_1_out, not_1_out, not_2_out, not_3_out, not_4_out, notx0notx1_out, notx1notx2_out, notx1x3_out,
       or_1_out, or_2_out, or_3_out, x0_out, x0x1_out, x1_out, x2_out, x2notx3_out, x3_out;

  Clock #(.highDuration(8), .lowDuration(8)) x3 (.out(x3_out));
  Clock #(.highDuration(4), .lowDuration(4)) x2 (.out(x2_out));
  Clock #(.highDuration(2), .lowDuration(2)) x1 (.out(x1_out));
  Clock x0 (.out(x0_out));
  not not_1 (not_1_out, x3_out);
  not not_2 (not_2_out, x2_out);
  not not_3 (not_3_out, x1_out);
  not not_4 (not_4_out, x0_out);
  and x0x1 (x0x1_out, x1_out, x0_out);
  and x2notx3 (x2notx3_out, not_1_out, x2_out);
  and notx1x3 (notx1x3_out, x3_out, not_3_out);
  and notx0notx1 (notx0notx1_out, not_3_out, not_4_out);
  and and_1 (and_1_out, x0x1_out, x2notx3_out);
  and notx1notx2 (notx1notx2_out, not_2_out, not_3_out);
  or or_1 (or_1_out, and_1_out, notx1x3_out);
  or or_2 (or_2_out, notx1notx2_out, notx0notx1_out);
  or or_3 (or_3_out, or_1_out, or_2_out);
  LED led_1 (.in(or_3_out));
endmodule
