// Logisim project DZ2.circ as structural Verilog: 2 circuits, main circuit main
module main (
  input  preset
);

  wire and_1_out, dtrigger_1_notq, dtrigger_1_q, dtrigger_2_notq, dtrigger_2_q, dtrigger_3_notq,
       dtrigger_3_q, dtrigger_4_notq, dtrigger_4_q, dtrigger_5_q, not_1_out, not_2_out, not_3_out, not_4_out,
       not_5_out, x1_1_out;

  Clock x1_1 (.out(x1_1_out));
  not not_1 (not_1_out, x1_1_out);
  LED Q0 (.in(dtrigger_1_q));
  DTrigger dtrigger_1 (
    .Preset(preset), .C(not_1_out), .D(dtrigger_1_notq), .Reset(and_1_out), .Q(dtrigger_1_q),
    .notQ(dtrigger_1_notq));
  LED Q1 (.in(dtrigger_2_q));
  LED Q2 (.in(dtrigger_3_q));
  not not_2 (not_2_out, dtrigger_1_q);
  LED Q3 (.in(dtrigger_4_q));
  DTrigger dtrigger_2 (
    .Preset(preset), .C(not_2_out), .D(dtrigger_2_notq), .Reset(and_1_out), .Q(dtrigger_2_q),
    .notQ(dtrigger_2_notq));
  not not_3 (not_3_out, dtrigger_2_q);
  DTrigger dtrigger_3 (
    .Preset(preset), .C(not_3_out), .D(dtrigger_3_notq), .Reset(and_1_out), .Q(dtrigger_3_q),
    .notQ(dtrigger_3_notq));
  not not_4 (not_4_out, dtrigger_3_q);
  and and_1 (and_1_out, dtrigger_3_q, dtrigger_4_q);
  not not_5 (not_5_out, and_1_out);
  DTrigger dtrigger_4 (
    .Preset(preset), .C(not_4_out), .D(dtrigger_4_notq), .Reset(dtrigger_5_q), .Q(dtrigger_4_q),
    .notQ(dtrigger_4_notq));
  DTrigger dtrigger_5 (.C(and_1_out), .D(1'b1), .Reset(not_5_out), .Q(dtrigger_5_q));  // open: Preset, notQ
endmodule

module DTrigger (
  input  Preset,
  input  C,
  input  D,
  input  Reset,
  output Q,
  output notQ
);

  wire nand_1_out, nand_2_out, nand_3_out, nand_4_out, not_1_out, not_2_out;

  not not_1 (not_1_out, Preset);
  not not_2 (not_2_out, Reset);
  nand nand_1 (nand_1_out, not_1_out, nand_4_out, nand_2_out);
  nand nand_2 (nand_2_out, nand_1_out, C, not_2_out);
  nand nand_3 (nand_3_out, C, nand_4_out, nand_2_out);
  nand nand_4 (nand_4_out, D, nand_3_out, not_2_out);
  nand nand_5 (Q, not_1_out, nand_2_out, notQ);
  nand nand_6 (notQ, Q, nand_3_out, not_2_out);
endmodule
