// Logisim project sqrt.circ as structural Verilog: 2 circuits, main circuit sqrt4bit
module sqrt8bit (
  input  A,
  input  B,
  input  C,
  input  D,
  input  E,
  input  F,
  input  G,
  input  H,
  output F3,
  output F2,
  output F1,
  output F0
);

  wire and_1_out, and_2_out, and_3_out, and_4_out, and_5_out, and_6_out, and_7_out, and_8_out, and_9_out,
       and_10_out, and_11_out, and_12_out, and_13_out, and_14_out, and_15_out, and_16_out, and_17_out,
       and_18_out, and_19_out, and_20_out, and_21_out, and_22_out, and_23_out, and_24_out, and_25_out,
       and_26_out, and_27_out, and_28_out, and_29_out, and_30_out, and_31_out, and_32_out, and_33_out,
       and_34_out, and_35_out, and_36_out, and_37_out, and_38_out, and_39_out, and_40_out, not_1_out,
       not_2_out, not_3_out, not_4_out, not_5_out, not_6_out;

  not not_1 (not_1_out, A);
  not not_2 (not_2_out, B);
  not not_3 (not_3_out, C);
  not not_4 (not_4_out, D);
  not not_5 (not_5_out, E);
  not not_6 (not_6_out, F);
  or or_1 (F3, B, A);
  and and_1 (and_1_out, not_2_out, D);
  and and_2 (and_2_out, not_2_out, C);
  and and_3 (and_3_out, A, B);
  and and_4 (and_4_out, not_2_out, not_3_out, not_4_out, F);
  and and_5 (and_5_out, not_2_out, not_3_out, not_4_out, E);
  and and_6 (and_6_out, not_1_out, C, F);
  and and_7 (and_7_out, not_1_out, C, E);
  and and_8 (and_8_out, not_1_out, C, D);
  and and_9 (and_9_out, A, not_2_out, not_3_out, not_4_out);
  and and_10 (and_10_out, A, B, F);
  and and_11 (and_11_out, A, B, E);
  and and_12 (and_12_out, A, B, D);
  and and_13 (and_13_out, A, B, C);
  and and_14 (and_14_out, not_2_out, not_3_out, not_4_out, not_6_out, H);
  and and_15 (and_15_out, not_2_out, not_3_out, not_4_out, not_6_out, G);
  and and_16 (and_16_out, not_1_out, not_2_out, not_3_out, E, H);
  and and_17 (and_17_out, not_1_out, not_2_out, not_3_out, E, G);
  and and_18 (and_18_out, not_2_out, not_3_out, not_4_out, E, F);
  and and_19 (and_19_out, not_1_out, D, E, H);
  and and_20 (and_20_out, not_1_out, D, E, G);
  and and_21 (and_21_out, not_1_out, D, E, F);
  and and_22 (and_22_out, not_1_out, C, not_4_out, not_5_out, not_6_out);
  and and_23 (and_23_out, not_2_out, C, D, H);
  and and_24 (and_24_out, not_2_out, C, D, G);
  and and_25 (and_25_out, not_2_out, C, D, F);
  and and_26 (and_26_out, not_2_out, C, D, E);
  and and_27 (and_27_out, not_1_out, B, not_3_out, D, H);
  and and_28 (and_28_out, not_1_out, B, not_3_out, D, G);
  and and_29 (and_29_out, not_1_out, B, not_3_out, D, F);
  and and_30 (and_30_out, not_1_out, B, not_3_out, D, E);
  and and_31 (and_31_out, A, not_2_out, not_3_out, not_4_out);
  and and_32 (and_32_out, A, not_3_out, not_4_out, not_5_out, not_6_out);
  and and_33 (and_33_out, A, C, E, H);
  and and_34 (and_34_out, A, C, E, G);
  and and_35 (and_35_out, A, C, E, F);
  and and_36 (and_36_out, A, C, D);
  and and_37 (and_37_out, A, B, C, H);
  and and_38 (and_38_out, A, B, C, G);
  and and_39 (and_39_out, A, B, C, F);
  and and_40 (and_40_out, A, B, C, E);
  or or_2 (F2, and_1_out, and_2_out, and_3_out);
  or or_3 (F1, and_4_out, and_5_out, and_6_out, and_7_out, and_8_out, and_9_out, and_10_out, and_11_out, and_12_out, and_13_out);
  or or_4 (F0, and_14_out, and_15_out, and_16_out, and_17_out, and_18_out, and_19_out, and_20_out, and_21_out, and_22_out, and_23_out, and_24_out, and_25_out, and_26_out, and_27_out, and_28_out, and_29_out, and_30_out, and_31_out, and_32_out, and_33_out, and_34_out, and_35_out, and_36_out, and_37_out, and_38_out, and_39_out, and_40_out);
endmodule

module sqrt4bit (
  input  D,
  input  C,
  input  B,
  input  A,
  output F0,
  output F1
);

  wire nand_1_out, nor_1_out, or_2_out;

  nand nand_1 (nand_1_out, D, C);
  or or_1 (F1, C, D);
  nor nor_1 (nor_1_out, B, A);
  or or_2 (or_2_out, C, nor_1_out);
  nand nand_2 (F0, nand_1_out, or_2_out);
endmodule
